# Fritzing sketch lechuck (saved by Fritzing 0.8.3b)

parts:
  R1 = Resistor [tolerance=±5% resistance=100 package=THT]
  S1 = Pushbutton [package="[THT]"]
  IC1 = IC, DIP package, 8 pins [chip_label="attiny 85"]
  VCC1 = Battery
  R2 = Resistor [tolerance=±5% resistance=100 package=THT]
  R3 = Resistor [tolerance=±5% resistance=100 package=THT]
  R4 = Resistor [tolerance=±5% resistance=100 package=THT]
  LED_0 = LED - 5mm [color="White (4500K)" package="5 mm [THT]"]
  LED2 = LED - 5mm [color="White (4500K)" package="5 mm [THT]"]
  LED3 = LED - 5mm [color="White (4500K)" package="5 mm [THT]"]
  LED4 = LED - 5mm [color="White (4500K)" package="5 mm [THT]"]
  LED5 = LED - 5mm [color="White (4500K)" package="5 mm [THT]"]
  LED6 = LED - 5mm [color="White (4500K)" package="5 mm [THT]"]
  LED7 = LED - 5mm [color="White (4500K)" package="5 mm [THT]"]
  LED8 = LED - 5mm [color="White (4500K)" package="5 mm [THT]"]
  LED9 = LED - 5mm [color="White (4500K)" package="5 mm [THT]"]
  LED10 = LED - 5mm [color="White (4500K)" package="5 mm [THT]"]
  LED11 = LED - 5mm [color="White (4500K)" package="5 mm [THT]"]
  LED12 = LED - 5mm [color="White (4500K)" package="5 mm [THT]"]

nets:
  N1: R1.Pin_0, IC1.pin6
  N2: R1.Pin_1, LED_0.cathode, LED2.anode, LED7.anode, LED8.cathode, LED9.anode, LED10.cathode
  N3: S1.Pin_3, S1.Pin_4, IC1.pin4, IC1.pin5, VCC1.-
  N4: IC1.pin2, R3.Pin_0
  N5: IC1.pin3, R4.Pin_0
  N6: IC1.pin7, R2.Pin_0
  N7: IC1.pin8, VCC1.+
  N8: R2.Pin_1, LED_0.anode, LED2.cathode, LED3.anode, LED4.cathode, LED5.anode, LED6.cathode
  N9: R3.Pin_1, LED3.cathode, LED4.anode, LED7.cathode, LED8.anode, LED11.anode, LED12.cathode
  N10: R4.Pin_1, LED5.cathode, LED6.anode, LED9.cathode, LED10.anode, LED11.cathode, LED12.anode

notes:
  LED 0
  LED 1
  LED 2
  LED 3
  LED 4
  LED 5
  LED 6
  LED 7
  LED 8
  LED 9
  LED 10
  LED 11
  Switch
